// Logisim project 16bit-cpu.circ as structural Verilog
module notgate (
  input  x,
  output notx
);

  nand nand_1 (notx, x, x);
endmodule

module andgate (
  input  a,
  input  b,
  output aandb
);

  wire nand_1_out;

  nand nand_1 (nand_1_out, a, b);
  notgate notgate_1 (.x(nand_1_out), .notx(aandb));
endmodule

module orgate (
  input  a,
  input  b,
  output aorb
);

  wire notgate_1_notx, notgate_2_notx;

  notgate notgate_1 (.x(a), .notx(notgate_1_notx));
  notgate notgate_2 (.x(b), .notx(notgate_2_notx));
  nand nand_1 (aorb, notgate_1_notx, notgate_2_notx);
endmodule

module xorgate (
  input  a,
  input  b,
  output axorb
);

  wire andgate_1_aandb, andgate_2_aandb, notgate_1_notx, notgate_2_notx;

  notgate notgate_1 (.x(a), .notx(notgate_1_notx));
  notgate notgate_2 (.x(b), .notx(notgate_2_notx));
  andgate andgate_1 (.a(notgate_1_notx), .b(b), .aandb(andgate_1_aandb));
  andgate andgate_2 (.a(a), .b(notgate_2_notx), .aandb(andgate_2_aandb));
  orgate orgate_1 (.a(andgate_1_aandb), .b(andgate_2_aandb), .aorb(axorb));
endmodule

module muxchip (
  input  b,
  input  sel,
  input  a,
  output muxout
);

  wire andgate_1_aandb, andgate_2_aandb, notgate_1_notx;

  andgate andgate_1 (.a(b), .b(sel), .aandb(andgate_1_aandb));
  notgate notgate_1 (.x(sel), .notx(notgate_1_notx));
  andgate andgate_2 (.a(notgate_1_notx), .b(a), .aandb(andgate_2_aandb));
  orgate orgate_1 (.a(andgate_1_aandb), .b(andgate_2_aandb), .aorb(muxout));
endmodule

module dmuxchip (
  input  x,
  input  sel,
  output a,
  output b
);

  wire notgate_1_notx;

  notgate notgate_1 (.x(sel), .notx(notgate_1_notx));
  andgate andgate_1 (.a(x), .b(notgate_1_notx), .aandb(a));
  andgate andgate_2 (.a(x), .b(sel), .aandb(b));
endmodule

module not16 (
  input  [15:0] a,
  output [15:0] nota
);

  notgate notgate_1 (.x(a[0]), .notx(nota[0]));
  notgate notgate_2 (.x(a[1]), .notx(nota[1]));
  notgate notgate_3 (.x(a[2]), .notx(nota[2]));
  notgate notgate_4 (.x(a[3]), .notx(nota[3]));
  notgate notgate_5 (.x(a[4]), .notx(nota[4]));
  notgate notgate_6 (.x(a[5]), .notx(nota[5]));
  notgate notgate_7 (.x(a[6]), .notx(nota[6]));
  notgate notgate_8 (.x(a[7]), .notx(nota[7]));
  notgate notgate_9 (.x(a[8]), .notx(nota[8]));
  notgate notgate_10 (.x(a[9]), .notx(nota[9]));
  notgate notgate_11 (.x(a[10]), .notx(nota[10]));
  notgate notgate_12 (.x(a[11]), .notx(nota[11]));
  notgate notgate_13 (.x(a[12]), .notx(nota[12]));
  notgate notgate_14 (.x(a[13]), .notx(nota[13]));
  notgate notgate_15 (.x(a[14]), .notx(nota[14]));
  notgate notgate_16 (.x(a[15]), .notx(nota[15]));
endmodule

module and16 (
  input  [15:0] a,
  input  [15:0] b,
  output [15:0] aandb
);

  assign aandb = a & b;  // AND_Gate and_1, 16 bits wide
endmodule

module or16 (
  input  [15:0] a,
  input  [15:0] b,
  output [15:0] aorb
);

  assign aorb = a | b;  // OR_Gate or_1, 16 bits wide
endmodule

module mux16 (
  input  [15:0] a,
  input  [15:0] b,
  input  sel,
  output [15:0] amuxb
);

  Multiplexer #(.width(16)) multiplexer_1 (.in0(a), .in1(b), .out(amuxb), .sel(sel));
endmodule

module or8way (
  input  in_1,
  input  in_2,
  input  in_3,
  input  in_4,
  input  in_5,
  input  in_6,
  input  in_7,
  input  in_8,
  output a8or
);

  or or_1 (a8or, in_1, in_2, in_3, in_4, in_5, in_6, in_7, in_8);
endmodule

module mux4way (
  input  a,
  input  b,
  input  c,
  input  d,
  input  [1:0] sel,
  output mux
);

  Multiplexer #(.select(2)) multiplexer_1 (.in0(a), .in1(b), .in2(c), .in3(d), .out(mux), .sel(sel));
endmodule

module mux8way (
  input  a,
  input  b,
  input  c,
  input  d,
  input  e,
  input  f,
  input  g,
  input  h,
  input  [2:0] sel,
  output out_10
);

  Multiplexer #(.select(3)) multiplexer_1 (
    .in0(a), .in1(b), .in2(c), .in3(d), .in4(e), .in5(f), .in6(g), .in7(h), .out(out_10), .sel(sel));
endmodule

module dmux4way (
  input  x,
  input  [1:0] sel,
  output a,
  output b,
  output c,
  output d
);

  Demultiplexer #(.select(2)) demultiplexer_1 (.out0(a), .out1(b), .out2(c), .out3(d), .in(x), .sel(sel));
endmodule

module dmux8way (
  input  x,
  input  [2:0] sel,
  output a,
  output b,
  output c,
  output d,
  output e,
  output f,
  output g,
  output h
);

  Demultiplexer #(.select(3)) demultiplexer_1 (
    .out0(a), .out1(b), .out2(c), .out3(d), .out4(e), .out5(f), .out6(g), .out7(h), .in(x), .sel(sel));
endmodule

module halfadder (
  input  a,
  input  b,
  output carry,
  output sum
);

  xor xor_1 (sum, a, b);
  and and_1 (carry, a, b);
endmodule

module fulladder (
  input  c,
  input  a,
  input  b,
  output sum,
  output carry
);

  wire halfadder_1_carry, halfadder_1_sum, halfadder_2_carry;

  halfadder halfadder_1 (.a(a), .b(b), .carry(halfadder_1_carry), .sum(halfadder_1_sum));
  halfadder halfadder_2 (.a(c), .b(halfadder_1_sum), .carry(halfadder_2_carry), .sum(sum));
  or or_1 (carry, halfadder_2_carry, halfadder_1_carry);
endmodule

module add16 (
  input  [15:0] a,
  input  [15:0] b,
  output [15:0] aplusb
);

  Adder #(.width(16)) adder_1 (.a(a), .b(b), .out(aplusb));  // open: cin, cout
endmodule

module inc16 (
  input  [15:0] a,
  output [15:0] ainc
);

  add16 add16_1 (.a(a), .b(16'h1), .aplusb(ainc));
endmodule

module alu (
  input  no,
  input  f,
  input  nx,
  input  ny,
  input  zx,
  input  zy,
  input  [15:0] x,
  input  [15:0] y,
  output [15:0] outt,
  output zr,
  output ng
);

  wire or8way_1_a8or, or8way_2_a8or;
  wire [15:0] add16_1_aplusb, and16_1_aandb, dmux16_1_a, dmux16_1_b, dmux16_2_a, dmux16_2_b, dmux16_3_a,
       dmux16_3_b, dmux16_4_a, dmux16_4_b, dmux16_5_a, dmux16_5_b, mux16_1_amuxb, mux16_2_amuxb,
       mux16_3_amuxb, mux16_4_amuxb, mux16_5_amuxb, not16_1_nota, not16_2_nota, not16_3_nota;

  mux16 mux16_1 (.a(x), .b({16{1'b0}}), .sel(zx), .amuxb(mux16_1_amuxb));
  mux16 mux16_2 (.a(y), .b({16{1'b0}}), .sel(zy), .amuxb(mux16_2_amuxb));
  dmux16 dmux16_1 (.x(mux16_1_amuxb), .sel(nx), .a(dmux16_1_a), .b(dmux16_1_b));
  dmux16 dmux16_2 (.x(mux16_2_amuxb), .sel(ny), .a(dmux16_2_a), .b(dmux16_2_b));
  not16 not16_1 (.a(dmux16_1_b), .nota(not16_1_nota));
  not16 not16_2 (.a(dmux16_2_b), .nota(not16_2_nota));
  mux16 mux16_3 (.a(dmux16_1_a), .b(not16_1_nota), .sel(nx), .amuxb(mux16_3_amuxb));
  mux16 mux16_4 (.a(dmux16_2_a), .b(not16_2_nota), .sel(ny), .amuxb(mux16_4_amuxb));
  dmux16 dmux16_3 (.x(mux16_3_amuxb), .sel(f), .a(dmux16_3_a), .b(dmux16_3_b));
  dmux16 dmux16_4 (.x(mux16_4_amuxb), .sel(f), .a(dmux16_4_a), .b(dmux16_4_b));
  and16 and16_1 (.a(dmux16_3_a), .b(dmux16_4_a), .aandb(and16_1_aandb));
  add16 add16_1 (.a(dmux16_3_b), .b(dmux16_4_b), .aplusb(add16_1_aplusb));
  mux16 mux16_5 (.a(and16_1_aandb), .b(add16_1_aplusb), .sel(f), .amuxb(mux16_5_amuxb));
  dmux16 dmux16_5 (.x(mux16_5_amuxb), .sel(no), .a(dmux16_5_a), .b(dmux16_5_b));
  not16 not16_3 (.a(dmux16_5_b), .nota(not16_3_nota));
  mux16 mux16_6 (.a(dmux16_5_a), .b(not16_3_nota), .sel(no), .amuxb({ng, outt[14:0]}));
  or8way or8way_1 (
    .in_1(outt[0]), .in_2(outt[1]), .in_3(outt[2]), .in_4(outt[3]), .in_5(outt[4]), .in_6(outt[5]),
    .in_7(outt[6]), .in_8(outt[7]), .a8or(or8way_1_a8or));
  or8way or8way_2 (
    .in_1(outt[8]), .in_2(outt[9]), .in_3(outt[10]), .in_4(outt[11]), .in_5(outt[12]), .in_6(outt[13]),
    .in_7(outt[14]), .in_8(ng), .a8or(or8way_2_a8or));
  orgate orgate_1 (.a(or8way_1_a8or), .b(or8way_2_a8or), .aorb(zr));

  assign outt[15] = ng;
endmodule

module dmux16 (
  input  [15:0] x,
  input  sel,
  output [15:0] a,
  output [15:0] b
);

  Demultiplexer #(.width(16)) demultiplexer_1 (.out0(a), .out1(b), .in(x), .sel(sel));
endmodule

module \bit  (
  input  x,
  input  load,
  output outt
);

  wire clock_1_out, multiplexer_1_out;

  Multiplexer multiplexer_1 (.in0(outt), .in1(x), .out(multiplexer_1_out), .sel(load));
  Clock clock_1 (.out(clock_1_out));
  D_Flip_Flop d_ff_1 (.D(multiplexer_1_out), .clk(clock_1_out), .Q(outt));  // open: Qn, preset, reset
endmodule

module registers (
);

  wire undriven;
  wire [15:0] multiplexer_1_out, multiplexer_2_out, register_1_q, register_2_q, register_3_q, register_4_q,
       register_5_q, register_6_q, register_7_q, register_8_q;

  Register #(.width(16)) register_1 (.en(undriven), .Q(register_1_q));  // open: D, clk, clr
  Register #(.width(16)) register_2 (.Q(register_2_q));  // open: D, en, clk, clr
  Register #(.width(16)) register_3 (.Q(register_3_q));  // open: D, en, clk, clr
  Register #(.width(16)) register_4 (.Q(register_4_q));  // open: D, en, clk, clr
  Register #(.width(16)) register_5 (.Q(register_5_q));  // open: D, en, clk, clr
  Register #(.width(16)) register_6 (.Q(register_6_q));  // open: D, en, clk, clr
  Register #(.width(16)) register_7 (.Q(register_7_q));  // open: D, en, clk, clr
  Register #(.width(16)) register_8 (.Q(register_8_q));  // open: D, en, clk, clr
  Multiplexer #(.select(3), .width(16)) multiplexer_1 (
    .in0(register_1_q), .in1(register_2_q), .in2(register_3_q), .in3(register_4_q), .in4(register_5_q),
    .in5(register_6_q), .in6(register_7_q), .in7(register_8_q), .out(multiplexer_1_out));  // open: sel
  Multiplexer #(.select(3), .width(16)) multiplexer_2 (
    .in0(register_1_q), .in1(register_2_q), .in2(register_3_q), .in3(register_4_q), .in4(register_5_q),
    .in5(register_6_q), .in6(register_7_q), .in7(register_8_q), .out(multiplexer_2_out));  // open: sel
endmodule

module cpu (
  input  [15:0] Instr,
  input  [15:0] inputt,
  input  reset,
  output [15:0] aluOut
);

  wire alu_1_ng, alu_1_zr, and_1_out, and_2_out, and_3_out, and_4_out, and_5_out, and_6_out, and_7_out,
       andgate_1_aandb, clock_1_out, not_1_out, not_2_out, notgate_1_notx, or_1_out, or_2_out, or_3_out,
       or_4_out, orgate_1_aorb;
  wire [15:0] adder_1_out, Areg_q, bit_extender_1_out, bit_extender_2_out, Dreg_q, multiplexer_1_out,
       multiplexer_2_out, multiplexer_3_out, multiplexer_4_out, multiplexer_5_out, register_1_q, undriven;

  notgate notgate_1 (.x(Instr[15]), .notx(notgate_1_notx));
  Multiplexer #(.width(16)) multiplexer_1 (.in0(Areg_q), .in1(inputt), .out(multiplexer_1_out), .sel(Instr[12]));
  andgate andgate_1 (.a(Instr[4]), .b(Instr[15]), .aandb(andgate_1_aandb));
  Multiplexer #(.width(16)) multiplexer_2 (.in0(Instr), .in1(aluOut), .out(multiplexer_2_out), .sel(Instr[15]));
  orgate orgate_1 (.a(notgate_1_notx), .b(Instr[5]), .aorb(orgate_1_aorb));
  alu alu_1 (
    .no(Instr[6]), .f(Instr[7]), .nx(Instr[10]), .ny(Instr[8]), .zx(Instr[11]), .zy(Instr[9]), .x(Dreg_q),
    .y(multiplexer_1_out), .outt(aluOut), .zr(alu_1_zr), .ng(alu_1_ng));
  Register #(.width(16)) Dreg (.D(aluOut), .en(andgate_1_aandb), .clk(clock_1_out), .Q(Dreg_q));  // open: clr
  not not_1 (not_1_out, alu_1_zr);
  not not_2 (not_2_out, alu_1_ng);
  and and_1 (and_1_out, alu_1_zr, 1'b1);
  and and_2 (and_2_out, alu_1_ng, 1'b1);
  Clock clock_1 (.out(clock_1_out));
  Register #(.width(16)) Areg (.D(multiplexer_2_out), .en(orgate_1_aorb), .clk(clock_1_out), .Q(Areg_q));  // open: clr
  and and_3 (and_3_out, not_1_out, not_2_out);
  and and_4 (and_4_out, and_2_out, Instr[0]);
  and and_5 (and_5_out, and_1_out, Instr[1]);
  and and_6 (and_6_out, and_3_out, Instr[2]);
  or or_1 (or_1_out, and_6_out, and_5_out);
  or or_2 (or_2_out, or_1_out, and_4_out);
  and and_7 (and_7_out, Instr[15], or_2_out);
  assign bit_extender_1_out = {{15{1'b1}}, 1'b1};  // Bit_Extender bit_extender_1
  Adder #(.width(16)) adder_1 (.a(bit_extender_1_out), .b(undriven), .out(adder_1_out));  // open: cin, cout
  Multiplexer #(.width(16)) multiplexer_3 (.in0(adder_1_out), .in1(undriven), .out(multiplexer_3_out), .sel(1'b1));
  Multiplexer #(.width(16)) multiplexer_4 (
    .in0(Areg_q), .in1(multiplexer_3_out), .out(multiplexer_4_out), .sel(and_7_out));
  assign bit_extender_2_out = {{15{1'b0}}, 1'b0};  // Bit_Extender bit_extender_2
  Multiplexer #(.width(16)) multiplexer_5 (
    .in0(bit_extender_2_out), .in1(multiplexer_4_out), .out(multiplexer_5_out), .sel(reset));
  or or_3 (or_3_out, and_7_out, reset);
  Register #(.width(16)) register_1 (.D(multiplexer_5_out), .en(or_4_out), .Q(register_1_q));  // open: clk, clr
  or or_4 (or_4_out, or_3_out, 1'b1);
endmodule
